# Fritzing sketch sketch (saved by Fritzing 0.9.3b)
breadboards: 1

parts:
  Part1 = Arduino Uno (Rev3) - ICSP
  DS1 = DS18B20 1-Wire Temperature Sensor [part_number=DS18B20]
  R1 = Resistor [tolerance=±5% resistance=4.7k package="0402 [SMD]"]
  Part2 = KY-019 5V Relay Module [package="Breakout board"]
  Part3 = Lilypad Battery Connect
  LED3 = LEDs [package=led10mm]

nets:
  N1: Part1.D2, DS1.DQ, R1.Pin_0
  N2: Part1.D4, Part2.S
  5V: Part1.5V, DS1.VDD, R1.Pin_1, Part2.+
  GND: Part1.GND, DS1.GND, Part2.-
  N3: Part2.NC, Part3.+
  N4: Part2.Common, LED3.A
  N5: Part3.-, LED3.C

notes:
  heating element

custom parts:
  KY-019 5V Relay Module: KY-019 5V Relay module, used to control AC circuits.
